// Logisim project 2_1.circ as structural Verilog: 1 circuit, main circuit main
module main (
  input  s,
  input  A,
  input  D,
  input  Up_Down,
  input  B,
  input  R,
  input  clk,
  input  D_2,
  output Q,
  output D_3,
  output Q_2,
  output Q_prime
);

  wire clock_1_out, clock_2_out, clock_3_out, multiplexer_1_out, not_1_out, not_2_out;
  wire [3:0] adder_1_out, D0_q, multiplexer_4_out;

  not not_1 (not_1_out, clk);
  Multiplexer multiplexer_1 (.in0(multiplexer_1_out), .in1(D_2), .out(multiplexer_1_out), .sel(clock_1_out));
  Clock clock_1 (.out(clock_1_out));
  not not_2 (not_2_out, clock_1_out);
  // Transmission_Gate transmission_1: pin names not known; wires that end beside it: A, clk, not_1_out, D_3
  // Transmission_Gate transmission_2: pin names not known; wires that end beside it: B, not_1_out, clk, D_3
  Multiplexer multiplexer_2 (.in0(Q_2), .in1(multiplexer_1_out), .out(Q_2), .sel(not_2_out));
  not not_3 (Q_prime, Q_2);
  Clock clock_2 (.out(clock_2_out));
  Multiplexer multiplexer_3 (.in0(Q), .in1(D), .out(Q), .sel(clock_2_out));
  D_Flip_Flop D0 (.D(adder_1_out[0]), .clk(clock_3_out), .Q(D0_q[0]), .preset(s), .reset(R));  // open: Qn
  D_Flip_Flop D1 (.D(adder_1_out[1]), .clk(clock_3_out), .Q(D0_q[1]), .preset(s), .reset(R));  // open: Qn
  Clock clock_3 (.out(clock_3_out));
  D_Flip_Flop D2 (.D(adder_1_out[2]), .clk(clock_3_out), .Q(D0_q[2]), .preset(s), .reset(R));  // open: Qn
  D_Flip_Flop D3 (.D(adder_1_out[3]), .clk(clock_3_out), .Q(D0_q[3]), .preset(s), .reset(R));  // open: Qn
  Multiplexer #(.width(4)) multiplexer_4 (.in0(4'b0001), .in1(4'b1111), .out(multiplexer_4_out), .sel(Up_Down));
  Adder #(.width(4)) adder_1 (.a(multiplexer_4_out), .b(D0_q), .out(adder_1_out), .cin(1'b0));  // open: cout

  // Notes on the sheet:
  //   clk
  //   2to1 MUX
  //   D-FF
  //   clk
  //   Latch
  //   clk
  //   Synchronous Up/Down Counter
endmodule
