// Logisim project 2_2.circ as structural Verilog: 1 circuit, main circuit main
module main (
  input  RST
);

  wire and_1_out, and_2_out, and_3_out, and_4_out, and_5_out, CLK_out, comparator_1_eq, comparator_1_gt,
       d_ff_1_q, decoder_1_out0, decoder_1_out1, decoder_1_out2, decoder_1_out3, decoder_1_out4,
       decoder_1_out5, decoder_1_out6, decoder_1_out7, decoder_1_out8, decoder_1_out9, decoder_1_out10,
       decoder_1_out11, decoder_1_out12, decoder_1_out13, decoder_1_out14, decoder_1_out15,
       multiplexer_3_out, nor_1_out, not_1_out, not_2_out, not_3_out, not_5_out, or_1_out, or_2_out,
       or_3_out, or_4_out;
  wire [3:0] bit_extender_1_out, multiplexer_2_out, PC_q, PC_q_2, PC_q_3;
  wire [11:0] adder_1_out, multiplexer_1_out;
  wire [11:4] multiplexer_2_out_2;
  wire [15:0] ACC_q, adder_2_out, IR_q, multiplexer_4_out, multiplexer_5_out, not_4_out, ram_1_dout;

  // Probe on decoder_1_out4
  // Probe on nor_1_out
  // Probe on decoder_1_out1
  D_Flip_Flop d_ff_1 (.D(not_1_out), .clk(CLK_out), .Q(d_ff_1_q), .reset(RST));  // open: Qn, preset
  not not_1 (not_1_out, d_ff_1_q);
  Clock CLK (.out(CLK_out));
  Hex_Digit_Display hex_digit_display_1 (.value(PC_q_3));  // open: dp
  Hex_Digit_Display hex_digit_display_2 (.value(PC_q_2));  // open: dp
  or or_1 (or_1_out, and_5_out, decoder_1_out4, and_4_out);
  Adder #(.width(12)) adder_1 (
    .a({PC_q_3, PC_q_2, PC_q}), .b({12{1'b0}}), .out(adder_1_out), .cin(1'b1));  // open: cout
  Multiplexer #(.width(12)) multiplexer_1 (
    .in0(adder_1_out), .in1(IR_q[11:0]), .out(multiplexer_1_out), .sel(or_1_out));
  or or_2 (or_2_out, and_4_out, decoder_1_out4, and_5_out, d_ff_1_q);
  and and_1 (and_1_out, or_2_out, nor_1_out);
  not not_2 (not_2_out, d_ff_1_q);
  Hex_Digit_Display hex_digit_display_3 (.value(PC_q));  // open: dp
  Register #(.width(12)) PC (
    .D(multiplexer_1_out), .en(and_1_out), .clk(CLK_out), .Q({PC_q_3, PC_q_2, PC_q}), .clr(RST));
  Multiplexer #(.width(12)) multiplexer_2 (
    .in0({PC_q_3, PC_q_2, PC_q}), .in1(IR_q[11:0]), .out({multiplexer_2_out_2, multiplexer_2_out}),
    .sel(d_ff_1_q));
  Hex_Digit_Display hex_digit_display_4 (.value(multiplexer_2_out_2[11:8]));  // open: dp
  // Probe on decoder_1_out0
  // Probe on decoder_1_out3
  // Probe on decoder_1_out2
  Hex_Digit_Display hex_digit_display_5 (.value(multiplexer_2_out));  // open: dp
  Hex_Digit_Display hex_digit_display_6 (.value(multiplexer_2_out_2[7:4]));  // open: dp
  not not_3 (not_3_out, CLK_out);
  Multiplexer multiplexer_3 (.in0(1'b0), .in1(1'b1), .out(multiplexer_3_out), .sel(decoder_1_out3));
  and and_2 (and_2_out, decoder_1_out1, not_3_out, d_ff_1_q);
  assign not_4_out = ~ram_1_dout;  // NOT_Gate not_4, 16 bits wide
  RAM #(.addrWidth(12), .asyncread("true"), .dataWidth(16)) ram_1 (
    .addr({multiplexer_2_out_2, multiplexer_2_out}), .we(and_2_out), .oe(1'b1), .clk(CLK_out), .din(ACC_q),
    .dout(ram_1_dout));
  Multiplexer #(.width(16)) multiplexer_4 (
    .in0(ACC_q), .in1({16{1'b0}}), .out(multiplexer_4_out), .sel(decoder_1_out0));
  Multiplexer #(.width(16)) multiplexer_5 (
    .in0(ram_1_dout), .in1(not_4_out), .out(multiplexer_5_out), .sel(multiplexer_3_out));
  // Probe on multiplexer_4_out
  Adder #(.width(16)) adder_2 (
    .a(multiplexer_4_out), .b(multiplexer_5_out), .out(adder_2_out), .cin(multiplexer_3_out));  // open: cout
  // Probe on multiplexer_5_out
  // Probe on adder_2_out
  or or_3 (or_3_out, decoder_1_out0, decoder_1_out3, decoder_1_out2);
  and and_3 (and_3_out, or_3_out, d_ff_1_q);
  Register #(.width(16)) ACC (.D(adder_2_out), .en(and_3_out), .clk(CLK_out), .Q(ACC_q), .clr(RST));
  // Probe on ram_1_dout
  Register #(.width(16)) IR (.D(ram_1_dout), .en(not_2_out), .clk(CLK_out), .Q(IR_q), .clr(RST));
  Hex_Digit_Display hex_digit_display_7 (.value(ACC_q[15:12]));  // open: dp
  Comparator #(.width(16)) comparator_1 (
    .a(ACC_q), .b({16{1'b0}}), .gt(comparator_1_gt), .eq(comparator_1_eq));  // open: lt
  Hex_Digit_Display hex_digit_display_8 (.value(ACC_q[11:8]));  // open: dp
  Hex_Digit_Display hex_digit_display_9 (.value(ACC_q[7:4]));  // open: dp
  // Probe on IR_q[11:0]
  assign bit_extender_1_out = {{3{1'b0}}, d_ff_1_q};  // Bit_Extender bit_extender_1
  or or_4 (or_4_out, comparator_1_gt, comparator_1_eq);
  not not_5 (not_5_out, comparator_1_eq);
  Hex_Digit_Display hex_digit_display_10 (.value(ACC_q[3:0]));  // open: dp
  Hex_Digit_Display OpCode (.value(IR_q[15:12]));  // open: dp
  Hex_Digit_Display hex_digit_display_11 (.value(bit_extender_1_out));  // open: dp
  // Probe on decoder_1_out5
  // Probe on decoder_1_out6
  Decoder #(.enable("false"), .select(4)) decoder_1 (
    .out0(decoder_1_out0), .out1(decoder_1_out1), .out2(decoder_1_out2), .out3(decoder_1_out3),
    .out4(decoder_1_out4), .out5(decoder_1_out5), .out6(decoder_1_out6), .out7(decoder_1_out7),
    .out8(decoder_1_out8), .out9(decoder_1_out9), .out10(decoder_1_out10), .out11(decoder_1_out11),
    .out12(decoder_1_out12), .out13(decoder_1_out13), .out14(decoder_1_out14), .out15(decoder_1_out15),
    .sel(IR_q[15:12]));
  and and_4 (and_4_out, or_4_out, decoder_1_out5);
  and and_5 (and_5_out, not_5_out, decoder_1_out6);
  nor nor_1 (nor_1_out, decoder_1_out7, decoder_1_out8, decoder_1_out9, decoder_1_out10, decoder_1_out11, decoder_1_out12, decoder_1_out13, decoder_1_out14, decoder_1_out15);

  // Notes on the sheet:
  //   MU0 Processor
  //   Program Counter
  //   Memory Address
  //   Accumulator Value
  //   Machine State
endmodule
